# Fritzing sketch Medidor_CO2 (saved by Fritzing 0.9.4)
breadboards: 1

parts:
  Componente2 = LCD1602-I2C
  Part1 = DHT22 Breakout module [package="Breakout board"]
  U1 = LuaNode32 / ESP32
  M1 = CCS811 Module [part_number=CJMCU-811]

nets:
  GND: Componente2.GND, Part1.-, U1.GND, M1.GND, M1.WAK
  VCC: Componente2.VCC, Part1.+, U1.Vin, M1.VCC
  N1: Componente2.SDA, U1.D21, M1.SDA
  N2: Componente2.SCL, U1.D22, M1.SCL
  N3: Part1.Out, U1.D14

custom parts:
  LCD1602-I2C: A standard character display, usually with 2x16 characters. Comes in many colors with LCM1602 IIC attached.
  DHT22 Breakout module: DHT22 temperature and humidity sensor module, provides a low-latency serial interface to measure humidity and temperature.
  LuaNode32 / ESP32: ESP32 based LuaNode32
  CCS811 Module: CCS811 Development Module The CCS811 is an ultra-low power digital gas sensor solution which integrates a metal oxide (MOX) gas sensor to detect a wide range of Volatile Organic Compounds (VOCs) for indoor air quality monitoring with a microcontroller unit (MCU), which includes an Analog-to-Digital converter (ADC), and an I2C interface. Links: CCS811 product datasheet
