# Fritzing sketch wemos_led_RGB (saved by Fritzing 0.9.9b)
breadboards: 1

parts:
  LED1 = RGB LED (com. cathode, rgb) [package="5 mm [THT]"]
  R2 = Resistor [tolerance=±5% resistance=220 package=THT]
  R3 = Resistor [tolerance=±5% resistance=220 package=THT]
  R4 = Resistor [tolerance=±5% resistance=220 package=THT]
  M1 = >Wemos D1 R32

nets:
  N1: LED1.red_anode, R2.Pin_1
  N2: LED1.common_cathode, M1.GND
  N3: LED1.green_anode, R3.Pin_1
  N4: LED1.blue_anode, R4.Pin_1
  N5: R2.Pin_0, M1.IO12
  N6: R3.Pin_0, M1.IO14
  N7: R4.Pin_0, M1.IO13
  N8: M1.SD1, M1.SD0

custom parts:
  RGB LED (com. cathode, rgb): A 5mm tri-color LED with red, green and blue inside.
  >Wemos D1 R32: Wemos D1 R32 - This board is used with dual-mode Wi-Fi and Bluetooth chips, which is safe, reliable, and scalable to a variety of applications. DC in 5V-12V, 1 analog input(3.2V max input), a Micro USB connection, Compatible with D1 R32=WiFi+bluetooth+UNO
